// Digital circuit 2_digits_mod_10_bcd.dig as structural Verilog
module _2_digits_mod_10_bcd (
  input  Clock,
  input  Reset,
  input  in_4,
  input  clk,
  input  in_6,
  output [15:0] Output_16
);

  wire and_1_out, and_2_out, and_3_out, and_4_out, multiplexer_1_out, or_1_out, or_2_out, or_3_out, or_4_out;

  Multiplexer multiplexer_1 (.sel(in_6), .in_0(clk), .in_1(Clock), .out(multiplexer_1_out));
  or or_1 (or_1_out, Reset, and_1_out);
  or or_2 (or_2_out, Reset, and_2_out);
  or or_3 (or_3_out, Reset, and_3_out);
  or or_4 (or_4_out, Reset, and_4_out);
  counter counter_1 (
    .Enable(in_4), .D_0(1'b0), .D_1(1'b0), .D_2(1'b0), .D_3(1'b0), .Load(or_1_out),
    .Clock(multiplexer_1_out), .Q_0(Output_16[0]), .Q_1(Output_16[1]), .Q_2(Output_16[2]), .Q_3(Output_16[3]));  // open: Z
  counter counter_2 (
    .Enable(and_1_out), .D_0(1'b0), .D_1(1'b0), .D_2(1'b0), .D_3(1'b0), .Load(or_2_out),
    .Clock(multiplexer_1_out), .Q_0(Output_16[4]), .Q_1(Output_16[5]), .Q_2(Output_16[6]), .Q_3(Output_16[7]));  // open: Z
  counter counter_3 (
    .Enable(and_2_out), .D_0(1'b0), .D_1(1'b0), .D_2(1'b0), .D_3(1'b0), .Load(or_3_out),
    .Clock(multiplexer_1_out), .Q_0(Output_16[8]), .Q_1(Output_16[9]), .Q_2(Output_16[10]),
    .Q_3(Output_16[11]));  // open: Z
  counter counter_4 (
    .Enable(and_3_out), .D_0(1'b0), .D_1(1'b0), .D_2(1'b0), .D_3(1'b0), .Load(or_4_out),
    .Clock(multiplexer_1_out), .Q_0(Output_16[12]), .Q_1(Output_16[13]), .Q_2(Output_16[14]),
    .Q_3(Output_16[15]));  // open: Z
  and and_1 (and_1_out, Output_16[3], Output_16[0]);
  and and_2 (and_2_out, Output_16[7], and_1_out, Output_16[4]);
  and and_3 (and_3_out, Output_16[11], and_2_out, Output_16[8]);
  and and_4 (and_4_out, Output_16[15], and_3_out, Output_16[12]);

  // Notes on the sheet:
  //   clk: Hz: 5
endmodule
