// Digital circuit 7LED_transcoder.dig as structural Verilog
module _7LED_transcoder (
  input  D_2,
  input  C_2,
  input  B_2,
  input  A_2,
  output a,
  output b,
  output c,
  output d,
  output e,
  output f,
  output g
);

  wire and_1_out, and_2_out, and_3_out, and_4_out, and_5_out, and_6_out, and_7_out, and_8_out, and_9_out,
       and_10_out, and_11_out, and_12_out, and_13_out, and_14_out, and_15_out, and_16_out, not_1_out,
       not_2_out, not_3_out;

  not not_1 (not_1_out, C_2);
  not not_2 (not_2_out, B_2);
  not not_3 (not_3_out, A_2);
  and and_1 (and_1_out, not_3_out, not_1_out);
  and and_2 (and_2_out, A_2, C_2);
  and and_3 (and_3_out, not_3_out, not_2_out);
  and and_4 (and_4_out, A_2, B_2);
  or or_1 (c, A_2, not_2_out, C_2);
  and and_5 (and_5_out, not_3_out, not_1_out);
  and and_6 (and_6_out, A_2, not_2_out, C_2);
  and and_7 (and_7_out, not_3_out, B_2);
  and and_8 (and_8_out, B_2, not_1_out);
  and and_9 (and_9_out, not_3_out, not_1_out);
  and and_10 (and_10_out, not_3_out, B_2);
  and and_11 (and_11_out, not_3_out, not_2_out);
  and and_12 (and_12_out, not_3_out, C_2);
  and and_13 (and_13_out, not_2_out, C_2);
  and and_14 (and_14_out, not_3_out, B_2);
  and and_15 (and_15_out, B_2, not_1_out);
  and and_16 (and_16_out, not_2_out, C_2);
  or or_2 (b, and_3_out, and_4_out, not_1_out);
  or or_3 (e, and_9_out, and_10_out);
  or or_4 (a, and_1_out, and_2_out, B_2, D_2);
  or or_5 (d, and_5_out, and_6_out, and_7_out, and_8_out, D_2);
  or or_6 (f, and_11_out, and_12_out, and_13_out, D_2);
  or or_7 (g, and_14_out, and_15_out, and_16_out, D_2);
endmodule
