// Digital circuit Address_generator_2b.dig as structural Verilog
module Address_generator_2b (
  input  Enable,
  input  Clock,
  input  Reset,
  output [1:0] Address
);

  wire and_1_out, or_1_out;

  or or_1 (or_1_out, and_1_out, Reset);
  counter counter_1 (
    .Enable(Enable), .D_0(1'b0), .D_1(1'b0), .D_2(1'b0), .D_3(1'b0), .Load(or_1_out), .Clock(Clock),
    .Q_0(Address[0]), .Q_1(Address[1]));  // open: Q_2, Q_3, Z
  and and_1 (and_1_out, Address[0], Enable, Address[1]);
endmodule
