// Digital circuit BCD_16b_counter.dig as structural Verilog
module BCD_16b_counter (
  input  Enable,
  input  Clock,
  input  Reset,
  output [15:0] Output_16
);

  wire and_1_out, and_2_out, and_3_out, and_4_out, or_1_out, or_2_out, or_3_out, or_4_out;

  or or_1 (or_1_out, Reset, and_1_out);
  or or_2 (or_2_out, Reset, and_2_out);
  or or_3 (or_3_out, Reset, and_3_out);
  or or_4 (or_4_out, Reset, and_4_out);
  counter counter_1 (
    .Enable(Enable), .D_0(1'b0), .D_1(1'b0), .D_2(1'b0), .D_3(1'b0), .Load(or_1_out), .Clock(Clock),
    .Q_0(Output_16[0]), .Q_1(Output_16[1]), .Q_2(Output_16[2]), .Q_3(Output_16[3]));  // open: Z
  counter counter_2 (
    .Enable(and_1_out), .D_0(1'b0), .D_1(1'b0), .D_2(1'b0), .D_3(1'b0), .Load(or_2_out), .Clock(Clock),
    .Q_0(Output_16[4]), .Q_1(Output_16[5]), .Q_2(Output_16[6]), .Q_3(Output_16[7]));  // open: Z
  counter counter_3 (
    .Enable(and_2_out), .D_0(1'b0), .D_1(1'b0), .D_2(1'b0), .D_3(1'b0), .Load(or_3_out), .Clock(Clock),
    .Q_0(Output_16[8]), .Q_1(Output_16[9]), .Q_2(Output_16[10]), .Q_3(Output_16[11]));  // open: Z
  counter counter_4 (
    .Enable(and_3_out), .D_0(1'b0), .D_1(1'b0), .D_2(1'b0), .D_3(1'b0), .Load(or_4_out), .Clock(Clock),
    .Q_0(Output_16[12]), .Q_1(Output_16[13]), .Q_2(Output_16[14]), .Q_3(Output_16[15]));  // open: Z
  and and_1 (and_1_out, Output_16[3], Enable, Output_16[0]);
  and and_2 (and_2_out, Output_16[7], and_1_out, Output_16[4]);
  and and_3 (and_3_out, Output_16[11], and_2_out, Output_16[8]);
  and and_4 (and_4_out, Output_16[15], and_3_out, Output_16[12]);

  // Notes on the sheet:
  //   loads[0]
  //   loads[1]
  //   loads[2]
  //   loads[3]
  //   steps[0]
  //   steps[1]
  //   steps[2]
  //   steps[3]
endmodule
