// Digital circuit Clk_div_1.10.dig as structural Verilog
module Clk_div_1_10 (
  input  Clock,
  input  Reset,
  output Output
);

  wire counter_1_q_0, counter_1_q_3, or_1_out;

  or or_1 (or_1_out, Output, Reset);
  counter counter_1 (
    .Enable(1'b1), .D_0(1'b0), .D_1(1'b0), .D_2(1'b0), .D_3(1'b0), .Load(or_1_out), .Clock(Clock),
    .Q_0(counter_1_q_0), .Q_3(counter_1_q_3));  // open: Q_1, Q_2, Z
  and and_1 (Output, counter_1_q_0, counter_1_q_3);
endmodule
