// Digital circuit Clk_div_1.100.dig as structural Verilog
module Clk_div_1_100 (
  input  Clock,
  input  Reset,
  output Output
);

  wire counter_1_q_2, counter_1_z, counter_2_q_1, counter_2_q_2, or_1_out;

  or or_1 (or_1_out, Output, Reset);
  counter counter_1 (
    .Enable(1'b1), .D_0(1'b0), .D_1(1'b0), .D_2(1'b0), .D_3(1'b0), .Load(or_1_out), .Clock(Clock),
    .Q_2(counter_1_q_2), .Z(counter_1_z));  // open: Q_0, Q_1, Q_3
  counter counter_2 (
    .Enable(counter_1_z), .D_0(1'b0), .D_1(1'b0), .D_2(1'b0), .D_3(1'b0), .Load(or_1_out), .Clock(Clock),
    .Q_1(counter_2_q_1), .Q_2(counter_2_q_2));  // open: Q_0, Q_3, Z
  and and_1 (Output, counter_1_q_2, counter_2_q_1, counter_2_q_2);
endmodule
