// Digital circuit Clk_div_1.1000.dig as structural Verilog
module Clk_div_1_1000 (
  input  Clock,
  input  Reset,
  output Output
);

  wire and_1_out, and_2_out, counter_1_q_3, counter_1_z, counter_2_q_1, counter_2_q_2, counter_2_q_3,
       counter_2_z, counter_3_q_0, counter_3_q_1, or_1_out;

  or or_1 (or_1_out, Output, Reset);
  counter counter_1 (
    .Enable(1'b1), .D_0(1'b0), .D_1(1'b0), .D_2(1'b0), .D_3(1'b0), .Load(or_1_out), .Clock(Clock),
    .Q_3(counter_1_q_3), .Z(counter_1_z));  // open: Q_0, Q_1, Q_2
  counter counter_2 (
    .Enable(counter_1_z), .D_0(1'b0), .D_1(1'b0), .D_2(1'b0), .D_3(1'b0), .Load(or_1_out), .Clock(Clock),
    .Q_1(counter_2_q_1), .Q_2(counter_2_q_2), .Q_3(counter_2_q_3), .Z(counter_2_z));  // open: Q_0
  counter counter_3 (
    .Enable(counter_2_z), .D_0(1'b0), .D_1(1'b0), .D_2(1'b0), .D_3(1'b0), .Load(or_1_out), .Clock(Clock),
    .Q_0(counter_3_q_0), .Q_1(counter_3_q_1));  // open: Q_2, Q_3, Z
  and and_1 (and_1_out, counter_2_q_1, counter_2_q_2, counter_2_q_3);
  and and_2 (and_2_out, counter_3_q_0, counter_3_q_1);
  and and_3 (Output, counter_1_q_3, and_1_out, and_2_out);
endmodule
