// Digital circuit Clk_div_1.16.dig as structural Verilog
module Clk_div_1_16 (
  input  Clock,
  input  Reset,
  output Output
);

  counter counter_1 (
    .Enable(1'b1), .D_0(1'b0), .D_1(1'b0), .D_2(1'b0), .D_3(1'b0), .Load(Reset), .Clock(Clock), .Z(Output));  // open: Q_0, Q_1, Q_2, Q_3

  // Notes on the sheet:
  //   Output: 1/16
endmodule
