// Digital circuit Rising_edge_detector.dig as structural Verilog
module Rising_edge_detector (
  input  Input,
  input  Clock,
  output Output
);

  wire d_ff_1_q, not_1_out;

  D_FF d_ff_1 (.D(Input), .C(Clock), .Q(d_ff_1_q));  // open: nQ
  not not_1 (not_1_out, d_ff_1_q);
  and and_1 (Output, Input, not_1_out);
endmodule
