// Digital circuit TC_7_led.dig as structural Verilog
module TC_7_led (
  input  clk,
  input  Reset,
  input  Input
);

  wire _7447_1_pin9, _7447_1_pin10, _7447_1_pin11, _7447_1_pin12, _7447_1_pin13, _7447_1_pin14,
       _7447_1_pin15, clk_div_1_100_1_output, decoder_1_out_0, decoder_1_out_1, decoder_1_out_2,
       decoder_1_out_3, rising_edge_detector_1_output;
  wire [1:0] address_generator_2b_1_address;
  wire [3:0] multiplexer_1_out;
  wire [15:0] bcd_16b_counter_1_output_16;

  Clk_div_1_100 clk_div_1_100_1 (.Clock(clk), .Reset(Reset), .Output(clk_div_1_100_1_output));
  Address_generator_2b address_generator_2b_1 (
    .Enable(clk_div_1_100_1_output), .Clock(clk), .Reset(Reset), .Address(address_generator_2b_1_address));
  Rising_edge_detector rising_edge_detector_1 (.Input(Input), .Clock(clk), .Output(rising_edge_detector_1_output));
  BCD_16b_counter bcd_16b_counter_1 (
    .Enable(rising_edge_detector_1_output), .Clock(clk), .Reset(Reset),
    .Output_16(bcd_16b_counter_1_output_16));
  Decoder #(.Selector_Bits(2)) decoder_1 (
    .sel(address_generator_2b_1_address), .out_0(decoder_1_out_0), .out_1(decoder_1_out_1),
    .out_2(decoder_1_out_2), .out_3(decoder_1_out_3));
  Multiplexer #(.Selector_Bits(2), .Bits(4)) multiplexer_1 (
    .sel(address_generator_2b_1_address), .in_0(bcd_16b_counter_1_output_16[3:0]),
    .in_1(bcd_16b_counter_1_output_16[7:4]), .in_2(bcd_16b_counter_1_output_16[11:8]),
    .in_3(bcd_16b_counter_1_output_16[15:12]), .out(multiplexer_1_out));
  _7447 _7447_1 (
    .pin1(multiplexer_1_out[1]), .pin2(multiplexer_1_out[2]), .pin3(1'b1), .pin4(1'b1), .pin5(1'b1),
    .pin6(multiplexer_1_out[3]), .pin7(multiplexer_1_out[0]), .pin8(1'b0), .pin9(_7447_1_pin9),
    .pin10(_7447_1_pin10), .pin11(_7447_1_pin11), .pin12(_7447_1_pin12), .pin13(_7447_1_pin13),
    .pin14(_7447_1_pin14), .pin15(_7447_1_pin15), .pin16(1'b1));
  Seven_Seg #(.commonCathode("true"), .commonConnectionType("anode"), .persistTime(16)) seven_seg_1 (
    .a(_7447_1_pin13), .b(_7447_1_pin12), .c(_7447_1_pin11), .d(_7447_1_pin10), .e(_7447_1_pin9),
    .f(_7447_1_pin15), .g(_7447_1_pin14), .dp(1'b1), .common(decoder_1_out_3));
  Seven_Seg #(.commonCathode("true"), .commonConnectionType("anode"), .persistTime(16)) seven_seg_2 (
    .a(_7447_1_pin13), .b(_7447_1_pin12), .c(_7447_1_pin11), .d(_7447_1_pin10), .e(_7447_1_pin9),
    .f(_7447_1_pin15), .g(_7447_1_pin14), .dp(1'b1), .common(decoder_1_out_2));
  Seven_Seg #(.commonCathode("true"), .commonConnectionType("anode"), .persistTime(16)) seven_seg_3 (
    .a(_7447_1_pin13), .b(_7447_1_pin12), .c(_7447_1_pin11), .d(_7447_1_pin10), .e(_7447_1_pin9),
    .f(_7447_1_pin15), .g(_7447_1_pin14), .dp(1'b1), .common(decoder_1_out_1));
  Seven_Seg #(.commonCathode("true"), .commonConnectionType("anode"), .persistTime(16)) seven_seg_4 (
    .a(_7447_1_pin13), .b(_7447_1_pin12), .c(_7447_1_pin11), .d(_7447_1_pin10), .e(_7447_1_pin9),
    .f(_7447_1_pin15), .g(_7447_1_pin14), .dp(1'b1), .common(decoder_1_out_0));

  // Notes on the sheet:
  //   clk: Hz: 800
  //   Rising Edge Counter
endmodule
