// Digital circuit counter.dig as structural Verilog
module counter (
  input  Enable,
  input  D_0,
  input  D_1,
  input  D_2,
  input  D_3,
  input  Load,
  input  Clock,
  output Q_0,
  output Q_1,
  output Q_2,
  output Q_3,
  output Z
);

  wire and_1_out, and_2_out, and_3_out, multiplexer_1_out, multiplexer_2_out, multiplexer_3_out,
       multiplexer_4_out, xor_1_out, xor_2_out, xor_3_out, xor_4_out;

  and and_1 (and_1_out, Q_0, Enable);
  and and_2 (and_2_out, Q_1, and_1_out);
  and and_3 (and_3_out, Q_2, and_2_out);
  and and_4 (Z, Q_3, and_3_out);
  xor xor_1 (xor_1_out, Q_0, Enable);
  xor xor_2 (xor_2_out, Q_1, and_1_out);
  xor xor_3 (xor_3_out, Q_2, and_2_out);
  xor xor_4 (xor_4_out, Q_3, and_3_out);
  Multiplexer multiplexer_1 (.sel(Load), .in_0(xor_1_out), .in_1(D_0), .out(multiplexer_1_out));
  Multiplexer multiplexer_2 (.sel(Load), .in_0(xor_2_out), .in_1(D_1), .out(multiplexer_2_out));
  Multiplexer multiplexer_3 (.sel(Load), .in_0(xor_3_out), .in_1(D_2), .out(multiplexer_3_out));
  Multiplexer multiplexer_4 (.sel(Load), .in_0(xor_4_out), .in_1(D_3), .out(multiplexer_4_out));
  D_FF d_ff_1 (.D(multiplexer_1_out), .C(Clock), .Q(Q_0));  // open: nQ
  D_FF d_ff_2 (.D(multiplexer_2_out), .C(Clock), .Q(Q_1));  // open: nQ
  D_FF d_ff_3 (.D(multiplexer_3_out), .C(Clock), .Q(Q_2));  // open: nQ
  D_FF d_ff_4 (.D(multiplexer_4_out), .C(Clock), .Q(Q_3));  // open: nQ
endmodule
